# Fritzing sketch WeatherStation (saved by Fritzing 0.9.3b)
circuit board: 5cm x 5cm
breadboards: 1

parts:
  MCU = Arduino Nano (Rev3.0)
  DHT22 = Humidity and Temperature Sensor RHT03
  UV_sensor--_UVM-30A = GUVA-S12SD UV Light Sensor
  Light_sensor = BH1750
  JP1 = Header 4 [package=jst-4-pth]

nets:
  GND: MCU.GND, DHT22.GND_1, DHT22.GND_2, UV_sensor--_UVM-30A.GND, Light_sensor.GND, Light_sensor.ADDR, JP1.2
  N1: MCU.D2, DHT22.Data-signal
  N2: MCU.D10, JP1.3
  5V: MCU.5V, DHT22.Vcc, UV_sensor--_UVM-30A.5V, Light_sensor.VCC, JP1.1
  N3: MCU.A5, Light_sensor.SCL
  N4: MCU.A4, Light_sensor.SDA
  N5: MCU.A1, UV_sensor--_UVM-30A.Out
  N6: MCU.A0, JP1.4

notes:
  Water Fall sensor
  Weather Station Hardware

custom parts:
  GUVA-S12SD UV Light Sensor: Extend your light-sensing spectrum with this analog UV sensor module. It uses a UV photodiode, which can detect the 240-370nm range of light (which covers UVB and most of UVA spectrum). The signal level from the photodiode is very small, in the nano-ampere level, so we tossed on an opamp to amplify the signal to a more manageable volt-level.
  BH1750: Light Sensor
